// Logisim project full-adder.circ as structural Verilog: 3 circuits, main circuit full_adder
module full_adder (
  input  A,
  input  B,
  input  Carry_In,
  output Sum,
  output Carry_Out
);

  wire AB_out, AC_out, BC_out, xor_1_out;

  xor xor_1 (xor_1_out, A, B);
  and AB (AB_out, A, B);
  and BC (BC_out, B, Carry_In);
  and AC (AC_out, A, Carry_In);
  xor xor_2 (Sum, xor_1_out, Carry_In);
  or or_1 (Carry_Out, AB_out, BC_out, AC_out);

  // Notes on the sheet:
  //   XOR -> eXclusive OR
  //   AB+BC+AC -> A(B+C)+BC
endmodule

module mux (
  input  _0,
  input  _1,
  input  _2,
  input  _3,
  input  in_5,
  input  in_6,
  output out_7
);

  wire and_1_out, and_2_out, and_3_out, and_4_out;

  and and_1 (and_1_out, _0, ~in_5, ~in_6);  // AND_Gate
  and and_2 (and_2_out, _1, ~in_5, in_6);  // AND_Gate
  and and_3 (and_3_out, _2, in_5, ~in_6);  // AND_Gate
  and and_4 (and_4_out, _3, in_5, in_6);
  or or_1 (out_7, and_1_out, and_2_out, and_3_out, and_4_out);
endmodule

module full_adder_with_mux (
  input  in_1,
  input  A,
  input  B,
  input  C_prime_in,
  output Sum,
  output C_prime_out
);

  wire mux_1_out_7;

  mux mux_1 (._0(in_1), ._1(1'b1), ._2(1'b1), ._3(in_1), .in_5(A), .in_6(B), .out_7(mux_1_out_7));
  mux mux_2 (._0(in_1), ._1(1'b1), ._2(1'b1), ._3(in_1), .in_5(mux_1_out_7), .in_6(C_prime_in), .out_7(Sum));
  mux mux_3 (._0(in_1), ._1(C_prime_in), ._2(C_prime_in), ._3(1'b1), .in_5(A), .in_6(B), .out_7(C_prime_out));
endmodule
