// Logisim project mux.circ as structural Verilog: 3 circuits, main circuit mux_8:1
module mux_4_1 (
  input  _0,
  input  _1,
  input  _2,
  input  _3,
  input  in_5,
  input  in_6,
  output Output
);

  wire and_1_out, and_2_out, and_3_out, and_4_out;

  and and_1 (and_1_out, _0, ~in_5, ~in_6);  // AND_Gate
  and and_2 (and_2_out, _1, ~in_5, in_6);  // AND_Gate
  and and_3 (and_3_out, _2, in_5, ~in_6);  // AND_Gate
  and and_4 (and_4_out, _3, in_5, in_6);
  or or_1 (Output, and_1_out, and_2_out, and_3_out, and_4_out);
endmodule

module mux_8_1 (
  input  _0,
  input  _1,
  input  _2,
  input  _3,
  input  _4,
  input  _5,
  input  _6,
  input  _7,
  input  S_prime_2,
  input  S_prime_1,
  input  S_prime_0,
  output Output
);

  wire and_1_out, and_2_out, and_3_out, and_4_out, and_5_out, and_6_out, and_7_out, and_8_out;

  and and_1 (and_1_out, _0, ~S_prime_2, ~S_prime_1, ~S_prime_0);  // AND_Gate
  and and_2 (and_2_out, _1, ~S_prime_2, ~S_prime_1, S_prime_0);  // AND_Gate
  and and_3 (and_3_out, _2, ~S_prime_2, S_prime_1, ~S_prime_0);  // AND_Gate
  and and_4 (and_4_out, _3, ~S_prime_2, S_prime_1, S_prime_0);  // AND_Gate
  and and_5 (and_5_out, _4, S_prime_2, ~S_prime_1, ~S_prime_0);  // AND_Gate
  and and_6 (and_6_out, _5, S_prime_2, ~S_prime_1, S_prime_0);  // AND_Gate
  and and_7 (and_7_out, _6, S_prime_2, S_prime_1, ~S_prime_0);  // AND_Gate
  and and_8 (and_8_out, _7, S_prime_2, S_prime_1, S_prime_0);
  or or_1 (Output, and_1_out, and_2_out, and_3_out, and_4_out, and_5_out, and_6_out, and_7_out, and_8_out);
endmodule

module mux_32_1 (
  input  _0,
  input  _1,
  input  _2,
  input  _3,
  input  _4,
  input  _5,
  input  _6,
  input  _7,
  input  _0_2,
  input  _1_2,
  input  _2_2,
  input  _3_2,
  input  _4_2,
  input  _5_2,
  input  _6_2,
  input  _7_2,
  input  _0_3,
  input  _1_3,
  input  _2_3,
  input  _3_3,
  input  _4_3,
  input  _5_3,
  input  _6_3,
  input  _7_3,
  input  _0_4,
  input  _1_4,
  input  _2_4,
  input  _3_4,
  input  _4_4,
  input  _5_4,
  input  _6_4,
  input  _7_4,
  input  in_33,
  input  in_34,
  input  in_35,
  input  in_36,
  input  in_37,
  output Output
);

  wire mux_8_1_1_output, mux_8_1_2_output, mux_8_1_3_output, mux_8_1_4_output;

  mux_8_1 mux_8_1_1 (
    ._0(_0), ._1(_1), ._2(_2), ._3(_3), ._4(_4), ._5(_5), ._6(_6), ._7(_7), .S_prime_2(in_35),
    .S_prime_1(in_36), .S_prime_0(in_37), .Output(mux_8_1_1_output));
  mux_8_1 mux_8_1_2 (
    ._0(_0_2), ._1(_1_2), ._2(_2_2), ._3(_3_2), ._4(_4_2), ._5(_5_2), ._6(_6_2), ._7(_7_2),
    .S_prime_2(in_35), .S_prime_1(in_36), .S_prime_0(in_37), .Output(mux_8_1_2_output));
  mux_8_1 mux_8_1_3 (
    ._0(_0_3), ._1(_1_3), ._2(_2_3), ._3(_3_3), ._4(_4_3), ._5(_5_3), ._6(_6_3), ._7(_7_3),
    .S_prime_2(in_35), .S_prime_1(in_36), .S_prime_0(in_37), .Output(mux_8_1_3_output));
  mux_8_1 mux_8_1_4 (
    ._0(_0_4), ._1(_1_4), ._2(_2_4), ._3(_3_4), ._4(_4_4), ._5(_5_4), ._6(_6_4), ._7(_7_4),
    .S_prime_2(in_35), .S_prime_1(in_36), .S_prime_0(in_37), .Output(mux_8_1_4_output));
  mux_4_1 mux_4_1_1 (
    ._0(mux_8_1_1_output), ._1(mux_8_1_2_output), ._2(mux_8_1_3_output), ._3(mux_8_1_4_output), .in_5(in_33),
    .in_6(in_34), .Output(Output));
endmodule
